# Fritzing sketch PCB (saved by Fritzing 0.9.3b)
breadboards: 1

parts:
  Part2 = Arduino Pro Mini (3.3V)  # not connected
  LED2 = smd LED [color="Blue (470nm)" package="0603 [SMD]"]  # not connected
  LED3 = smd LED [color="Blue (470nm)" package="0603 [SMD]"]  # not connected
  M1-hands = DC Motor  # not connected
  M2-legs = DC Motor
  S1 = Round Pushbutton  # not connected
  U1 = SWITCH_SPDT [package=kps-1290]  # not connected
  U2 = LIPO-1000mAh [package=lipo-1000]
  IR1 = TSOP312.., 314.. [package=THT]  # not connected
  IR2 = TSOP312.., 314.. [package=THT]  # not connected
  Q1 = TRANSISTOR_NPN [package=to-92-ammo]
  Q2 = PNP-Transistor [package="TO92 [THT]"]
  Q3 = PNP-Transistor [package="TO92 [THT]"]
  Q4 = TRANSISTOR_NPN [package=to-92-ammo]
  D2 = Diode [package=diode-1n4148]
  D3 = Diode [package=diode-1n4148]
  D4 = Diode [package=diode-1n4148]
  D5 = Diode [package=diode-1n4148]

nets:
  N1: M2-legs.pin_1, Q1.E, Q2.E, D2.A, D4.C
  N2: M2-legs.pin_2, Q3.E, Q4.E, D3.A, D5.C
  N3: U2.+, Q1.C, Q4.C, D2.C, D3.C
  N4: Q1.B, Q2.B
  N5: Q2.C, Q3.C, D4.A, D5.A
